# Fritzing sketch Ard_Rasp_Camera (saved by Fritzing 0.9.3b)
breadboards: 1

parts:
  Part1 = Arduino Uno (Rev3)
  Raspberry_Pi_1 = Raspberry Pi 3 [part_number=RPI-3-V1.2]  # not connected
  J1 = Basic Servo
  J2 = Basic Servo
  U1 = TCM8240MD [package=tcm8240md]  # not connected

nets:
  N1: Part1.D9_PWM, J1.vcc
  N2: Part1.D10_PWM/SS, J2.vcc
  N3: Part1.5V, J1.pulse, J2.pulse
  GND: Part1.GND, J1.gnd, J2.gnd
